// Logisim project cpu.circ as structural Verilog: 3 circuits, main circuit main
module main (
  input  [15:0] INSTRUCTION,
  input  CLOCK,
  output [15:0] FETCH_ADDRESS,
  output Overflow,
  output [15:0] s0_Value,
  output [15:0] s1_Value,
  output [15:0] s2_Value,
  output [15:0] ra_Value,
  output [15:0] sp_Value,
  output [15:0] HI_Value,
  output [15:0] LO_Value
);

  wire AluSrc, and_1_out, and_3_out, Branch, comparator_1_eq, comparator_2_eq, Equal, ExtOp, Jump, lui,
       MEM_p1, MEM_p2, MemToReg, MemWr, mfhi, mflo, Mult, no_nop, not_1_out, not_2_out, not_3_out, or_1_out,
       or_2_out, R, RegWr, shift, U_RegDst;
  wire [1:0] rd_2;
  wire [2:0] AluCtr, bit_extender_1_out, funct, RR2, Write_Address;
  wire [3:0] opcode;
  wire [5:3] imm_6;
  wire [9:0] prev_address;
  wire [9:6] J_imm;
  wire [15:0] address_2, ALU_A, ALU_B, Alu_Out_1, Alu_Out_2, ALU_Out_R, bit_extender_2_out,
       bit_extender_3_out, branch_address, i_extended_imm, Mem_Address, Mem_Write_Data, multiplexer_1_out,
       multiplexer_2_out, multiplexer_5_out, multiplexer_6_out, multiplexer_7_out, multiplexer_8_out,
       multiplexer_10_out, next_address, next_PC, RAMout, RamOut_t, shifter_1_out, u_extended_imm,
       Write_Data, WriteData;
  wire [15:10] jump_address;

  Multiplexer #(.width(16), .enable("false")) multiplexer_1 (
    .in0(address_2), .in1({jump_address, J_imm, imm_6, funct}), .out(multiplexer_1_out), .sel(Jump));
  Register #(.width(16)) PC (.D(next_PC), .Q(FETCH_ADDRESS), .clk(CLOCK));  // open: en, clr
  not not_1 (not_1_out, Jump);
  and and_1 (and_1_out, not_2_out, RegWr);
  not not_2 (not_2_out, Overflow);
  Adder #(.width(16)) adder_1 (.a(FETCH_ADDRESS), .b(16'h2), .out(address_2));  // open: cin, cout
  Adder #(.width(16)) adder_2 (.a(FETCH_ADDRESS), .b(16'hfffe), .out({jump_address, prev_address}));  // open: cin, cout
  Adder #(.width(16)) adder_3 (
    .a({jump_address, prev_address}), .b(i_extended_imm), .out(branch_address));  // open: cin, cout
  Multiplexer #(.width(16), .enable("false")) multiplexer_2 (
    .in0(multiplexer_1_out), .in1(branch_address), .out(multiplexer_2_out), .sel(Equal));
  Comparator #(.width(16)) comparator_1 (.a(next_address), .b(address_2), .eq(comparator_1_eq));  // open: gt, lt
  regfile_main main_1 (
    .Read_Register_1(J_imm[8:6]), .Read_Register_2(RR2), .Write_Register(Write_Address),
    .Write_Data(Write_Data), .Write_Enable(and_1_out), .Clock(CLOCK), .Read_Data_1(ALU_A),
    .Read_Data_2(Mem_Write_Data), .s0_Value(s0_Value), .s1_Value(s1_Value), .s2_Value(s2_Value),
    .ra_Value(ra_Value), .sp_Value(sp_Value));
  and and_2 (no_nop, comparator_1_eq, not_1_out);
  and and_3 (and_3_out, Jump, not_3_out);
  not not_3 (not_3_out, U_RegDst);
  Multiplexer #(.width(16), .enable("false")) multiplexer_3 (
    .in0(multiplexer_2_out), .in1(Mem_Address), .out(next_address), .sel(and_3_out));
  Register #(.width(16)) HI (.D(Alu_Out_2), .en(Mult), .Q(HI_Value), .clr(CLOCK));  // open: clk
  Multiplexer #(.width(16), .enable("false")) multiplexer_4 (
    .in0(Mem_Write_Data), .in1(i_extended_imm), .out(ALU_B), .sel(AluSrc));
  Multiplexer #(.width(16), .enable("false")) multiplexer_5 (
    .in0({16{1'b0}}), .in1(INSTRUCTION), .out(multiplexer_5_out), .sel(no_nop));
  Control_signal control_signal_1 (
    .Input({opcode, rd_2, J_imm, imm_6, funct}), .lui(lui), .Mult(Mult), .R(R), .RegWr(RegWr), .Jump(Jump),
    .Branch(Branch), .ExtOp(ExtOp), .AluSrc(AluSrc), .MemWrite(MemWr), .MemToReg(MemToReg), .AluCtr(AluCtr),
    .U_RegDst(U_RegDst), .shift(shift), .mfhi(mfhi), .mflo(mflo));
  Register #(.width(16)) register_1 (
    .D(multiplexer_5_out), .Q({opcode, rd_2, J_imm, imm_6, funct}), .clr(CLOCK));  // open: en, clk
  alu_main main_2 (
    .Switch(AluCtr), .X(ALU_A), .Equal(Equal), .Result(Alu_Out_1), .Y(ALU_B), .Result_2(Alu_Out_2),
    .Signed_Overflow(Overflow));
  Shifter #(.width(16)) shifter_1 (.in(u_extended_imm), .\dist (4'b0110), .out(shifter_1_out));
  Multiplexer #(.width(16), .enable("false")) multiplexer_6 (
    .in0(Alu_Out_1), .in1(shifter_1_out), .out(multiplexer_6_out), .sel(lui));
  or or_1 (or_1_out, lui, Mult);
  Register #(.width(16)) LO (.D(multiplexer_6_out), .en(or_1_out), .Q(LO_Value), .clr(CLOCK));  // open: clk
  Multiplexer #(.width(16), .enable("false")) multiplexer_7 (
    .in0(ALU_Out_R), .in1(FETCH_ADDRESS), .out(multiplexer_7_out), .sel(Jump));
  Comparator #(.width(4)) comparator_2 (.a(4'b1100), .b(opcode), .eq(comparator_2_eq));  // open: gt, lt
  assign bit_extender_1_out = {{1{1'b0}}, rd_2};  // Bit_Extender bit_extender_1
  Adder #(.width(16)) adder_4 (.a(ALU_A), .b(i_extended_imm), .out(Mem_Address));  // open: cin, cout
  Multiplexer #(.width(16), .enable("false")) multiplexer_8 (
    .in0(multiplexer_7_out), .in1(HI_Value), .out(multiplexer_8_out), .sel(mfhi));
  or or_2 (or_2_out, comparator_2_eq, Branch);
  Multiplexer #(.width(3), .enable("false")) multiplexer_9 (
    .in0({rd_2, J_imm[9]}), .in1(bit_extender_1_out), .out(Write_Address), .sel(U_RegDst));
  assign bit_extender_2_out = {{10{imm_6[5]}}, {imm_6, funct}};  // Bit_Extender bit_extender_2
  assign bit_extender_3_out = {{10{1'b0}}, {imm_6, funct}};  // Bit_Extender bit_extender_3
  assign u_extended_imm = {{6{1'b0}}, {J_imm, imm_6, funct}};  // Bit_Extender bit_extender_4
  // mem_main MEM: pin names not known; wires that end beside it: MEM_p1, MEM_p2, Mem_Address, Mem_Write_Data, MemWr, CLOCK, RamOut_t
  Multiplexer #(.width(16), .enable("false")) multiplexer_10 (
    .in0(multiplexer_8_out), .in1(LO_Value), .out(multiplexer_10_out), .sel(mflo));
  Multiplexer #(.width(3), .enable("false")) multiplexer_11 (
    .in0(imm_6), .in1({rd_2, J_imm[9]}), .out(RR2), .sel(or_2_out));
  Multiplexer #(.width(16), .enable("false")) multiplexer_12 (
    .in0(bit_extender_2_out), .in1(bit_extender_3_out), .out(i_extended_imm), .sel(ExtOp));
  Multiplexer #(.width(16), .enable("false")) multiplexer_13 (
    .in0(multiplexer_10_out), .in1(RAMout), .out(WriteData), .sel(MemToReg));

  // Other names for the same wires on the sheet: imm_6[2:0] = funct; J_imm[5:0] = {imm_6, funct};
  //   jump_address[9:0] = {J_imm, imm_6, funct}; rt[2:0] = imm_6; RR1[2:0] = J_imm[8:6]; rs[2:0] = J_imm[8:6];
  //   rd_3[2:0] = {rd_2, J_imm[9]}; clk = CLOCK; fetch_addr[15:0] = FETCH_ADDRESS; HI[15:0] = HI_Value;
  //   prev_address[15:10] = jump_address; LO[15:0] = LO_Value; R_s__Signext_imm[15:0] = Mem_Address;
  //   ra[15:0] = ra_Value; Read_Data_1[15:0] = ALU_A; Read_Data_2[15:0] = Mem_Write_Data; s0[15:0] = s0_Value;
  //   s1[15:0] = s1_Value; s2[15:0] = s2_Value; sp[15:0] = sp_Value

  // Notes on the sheet:
  //   Output
  //   Reg File
  //   next address?
  //   These are outputs/inputs from run.circ
  //   Inputs
  //   PC
  //   hi instruction
  //   These are DEBUG/TEST outputs from your circuit.
  //   low instruction
  //   ALU
  //   Memory
  //   sh
  //   immediate extension
endmodule

// Control_Signal
module Control_signal (
  input  [15:0] Input,
  output lui,
  output Mult,
  output R,
  output RegWr,
  output Jump,
  output Branch,
  output ExtOp,
  output AluSrc,
  output MemWrite,
  output MemToReg,
  output [2:0] AluCtr,
  output U_RegDst,
  output shift,
  output mfhi,
  output mflo
);

  wire addi, addiu, andi, beq, bne, j, jr, lh, or_4_out, ori, slti;
  wire [2:0] AluCtr_not_R;

  Multiplexer #(.select(4), .width(3)) multiplexer_1 (
    .in0(Input[2:0]), .in1(3'b000), .in2(3'b010), .in3(3'b010), .in4(3'b010), .in5(3'b010), .in6(3'b010),
    .in7(3'b101), .in8(3'b110), .in9(3'b011), .in10(3'b100), .in11(3'b010), .in12(3'b010),
    .out(AluCtr_not_R), .sel(Input[15:12]));  // open: in13, in14, in15, en
  and isRtype (R, ~Input[12], ~Input[13], ~Input[14], ~Input[15]);  // AND_Gate
  Multiplexer #(.width(3)) multiplexer_2 (.in0(AluCtr_not_R), .in1(Input[2:0]), .out(AluCtr), .sel(R));  // open: en
  and and_1 (shift, ~Input[2], R, ~Input[1]);  // AND_Gate
  and and_2 (lui, Input[12], ~Input[13], ~R, ~Input[14], ~Input[15]);  // AND_Gate
  and and_3 (beq, ~Input[15], Input[14], ~R, ~Input[13], ~Input[12]);  // AND_Gate
  and and_4 (j, ~Input[15], ~Input[14], ~R, Input[13], ~Input[12]);  // AND_Gate
  and and_5 (addi, ~Input[15], Input[14], R, Input[13], ~Input[12]);  // AND_Gate
  and and_6 (addiu, ~Input[15], Input[14], ~R, Input[13], Input[12]);  // AND_Gate
  and and_7 (slti, Input[15], ~Input[14], ~R, ~Input[13], ~Input[12]);  // AND_Gate
  and and_8 (Mult, R, Input[2], Input[0], Input[1]);
  and and_9 (mfhi, Input[15], Input[14], ~R, ~Input[13], Input[12]);  // AND_Gate
  and and_10 (mflo, Input[15], Input[14], ~R, Input[13], ~Input[12]);  // AND_Gate
  and and_11 (andi, Input[15], ~Input[14], ~R, ~Input[13], Input[12]);  // AND_Gate
  and and_12 (ori, Input[15], ~Input[14], R, Input[13], ~Input[12]);  // AND_Gate
  and and_13 (lh, Input[15], ~Input[14], ~R, Input[13], Input[12]);  // AND_Gate
  and and_14 (MemWrite, Input[15], Input[14], ~R, ~Input[13], ~Input[12]);  // AND_Gate
  and and_15 (bne, ~Input[15], Input[14], ~R, ~Input[13], Input[12]);  // AND_Gate
  and and_16 (jr, ~Input[15], ~Input[14], ~R, Input[13], Input[13]);  // AND_Gate
  or or_1 (Jump, j, jr);
  or or_2 (Branch, beq, bne);
  or or_3 (RegWr, R, lui, addi, addiu, mfhi, mflo, ori, lh);
  not not_1 (ExtOp, or_4_out);
  or or_4 (or_4_out, andi, ori);
  or or_5 (AluSrc, addi, ori, lh, andi, MemWrite, addiu);
  or or_6 (MemToReg, mflo, mfhi, lh);
  or or_7 (U_RegDst, j, lui);

  // Other names for the same wires on the sheet: sh = MemWrite

  // Notes on the sheet:
  //   sll
  //   addi
  //   and
  //   or
  //   addiu
  //   slti
endmodule

module PC (
  input  [15:0] PC,
  input  [9:0] J_imm,
  input  [5:0] imm_6,
  input  [3:0] opcode,
  input  equal,
  input  [15:0] R_s__Signext_imm,
  input  Jump,
  input  U,
  output [15:0] PC_2,
  output [15:0] Jump_Address,
  output [15:0] PC___2___SignExt_imm,
  output [15:0] NextPC,
  output Branch_Taken
);

  wire and_1_out, and_2_out, and_3_out, and_4_out, comparator_1_eq, comparator_2_eq;
  wire [15:0] adder_2_out, bit_extender_1_out, bit_extender_2_out, bit_extender_3_out, multiplexer_1_out,
       multiplexer_2_out, shifter_1_out;

  Adder #(.width(16)) adder_1 (.a(16'h2), .b(PC), .out(PC_2));  // open: cin, cout
  assign bit_extender_1_out = {{10{1'b0}}, PC[15:10]};  // Bit_Extender bit_extender_1
  assign bit_extender_2_out = {{10{imm_6[5]}}, imm_6};  // Bit_Extender bit_extender_2
  Comparator #(.width(4)) comparator_1 (.a(opcode), .b(4'b0100), .eq(comparator_1_eq));  // open: gt, lt
  Comparator #(.width(4)) comparator_2 (.a(opcode), .b(4'b0101), .eq(comparator_2_eq));  // open: gt, lt
  Shifter #(.width(16)) shifter_1 (.in(bit_extender_1_out), .\dist (4'b1010), .out(shifter_1_out));
  Adder #(.width(16)) adder_2 (.a(PC), .b(bit_extender_2_out), .out(adder_2_out));  // open: cin, cout
  and and_1 (and_1_out, comparator_1_eq, equal);
  and and_2 (and_2_out, comparator_2_eq, ~equal);  // AND_Gate
  assign bit_extender_3_out = {{6{1'b0}}, J_imm};  // Bit_Extender bit_extender_3
  Adder #(.width(16)) adder_3 (.a(16'h2), .b(adder_2_out), .out(PC___2___SignExt_imm));  // open: cin, cout
  Multiplexer #(.width(16), .enable("false")) multiplexer_1 (
    .in0(PC_2), .in1(PC___2___SignExt_imm), .out(multiplexer_1_out), .sel(Branch_Taken));
  or or_1 (Branch_Taken, and_1_out, and_2_out);
  Adder #(.width(16)) adder_4 (.a(shifter_1_out), .b(bit_extender_3_out), .out(Jump_Address));  // open: cin, cout
  Multiplexer #(.width(16), .enable("false")) multiplexer_2 (
    .in0(multiplexer_1_out), .in1(Jump_Address), .out(multiplexer_2_out), .sel(and_3_out));
  and and_3 (and_3_out, Jump, U);
  Multiplexer #(.width(16), .enable("false")) multiplexer_3 (
    .in0(multiplexer_2_out), .in1(R_s__Signext_imm), .out(NextPC), .sel(and_4_out));
  and and_4 (and_4_out, Jump, ~U);  // AND_Gate

  // Other names for the same wires on the sheet: J_address[15:0] = Jump_Address; next_PC[15:0] = NextPC;
  //   PC_Signext_imm[15:0] = PC___2___SignExt_imm
endmodule
