// Logisim project alu.circ as structural Verilog: 3 circuits, main circuit main
module main (
  input  [15:0] X,
  input  [15:0] Y,
  input  [2:0] Switch,
  output Equal,
  output [15:0] Result,
  output [15:0] Result_2,
  output Signed_Overflow
);

  wire comparator_2_eq, comparator_3_eq, OverFlow;
  wire [3:0] bit_extender_1_out, bit_extender_2_out;
  wire [15:0] result0, result1, result2, result3, result4, result5, result6, result7, result7_2;
  wire [31:0] bit_extender_3_out, bit_extender_4_out;

  Bit_Extender #(.in_width(16), .out_width(4)) bit_extender_1 (.in(Y), .out(bit_extender_1_out));
  Bit_Extender #(.in_width(16), .out_width(4)) bit_extender_2 (.in(Y), .out(bit_extender_2_out));
  assign bit_extender_3_out = {{16{1'b0}}, X};  // Bit_Extender bit_extender_3
  assign bit_extender_4_out = {{16{1'b0}}, Y};  // Bit_Extender bit_extender_4
  Shifter #(.width(16)) shifter_1 (.in(X), .\dist (bit_extender_1_out), .out(result0));
  Shifter #(.width(16), .shift("lr")) shifter_2 (.in(X), .\dist (bit_extender_2_out), .out(result1));
  Adder #(.width(16)) adder_1 (.a(X), .b(Y), .out(result2), .cout(OverFlow));  // open: cin
  assign result3 = X & Y;  // AND_Gate and_1, 16 bits wide
  assign result4 = X | Y;  // OR_Gate or_1, 16 bits wide
  Adder #(.width(16)) adder_2 (.a(X), .b(Y), .out(result5));  // open: cin, cout
  SLT slt_1 (.A(X), .B(Y), .Result(result6));
  Multiplier #(.width(32)) multiplier_1 (
    .a(bit_extender_3_out), .b(bit_extender_4_out), .out({result7_2, result7}));  // open: cin, cout
  Comparator #(.width(16)) comparator_1 (.a(X), .b(Y), .eq(Equal));  // open: gt, lt
  Comparator #(.width(3)) comparator_2 (.a(Switch), .b(3'b111), .eq(comparator_2_eq));  // open: gt, lt
  Comparator #(.width(3)) comparator_3 (.a(Switch), .b(3'b010), .eq(comparator_3_eq));  // open: gt, lt
  Multiplexer #(.width(16)) multiplexer_1 (
    .in0({16{1'b0}}), .in1(result7_2), .out(Result_2), .sel(comparator_2_eq));  // open: en
  Multiplexer multiplexer_2 (.in0(1'b0), .in1(OverFlow), .out(Signed_Overflow), .sel(comparator_3_eq));  // open: en
  Multiplexer #(.select(3), .width(16)) multiplexer_3 (
    .in0(result0), .in1(result1), .in2(result2), .in3(result3), .in4(result4), .in5(result5), .in6(result6),
    .in7(result7), .out(Result), .sel(Switch));  // open: en

  // Other names for the same wires on the sheet: overflow_t = Signed_Overflow; S[2:0] = Switch

  // Notes on the sheet:
  //   INPUTS to your circuit
  //   DON'T CHANGE THE LOCATIONS OF THE INPUTS AND OUTPUTS!
  //   OUTPUTS from your circuit
endmodule

module SLT (
  input  [15:0] A,
  input  [15:0] B,
  output [15:0] Result
);

  wire comparator_1_lt;

  Comparator #(.width(16)) comparator_1 (.a(A), .b(B), .lt(comparator_1_lt));  // open: gt, eq
  assign Result = {{15{1'b0}}, comparator_1_lt};  // Bit_Extender bit_extender_1
endmodule

module Equal (
  input  [15:0] A,
  input  [15:0] B,
  output [15:0] out
);

  wire comparator_1_eq;

  Comparator #(.width(16)) comparator_1 (.a(A), .b(B), .eq(comparator_1_eq));  // open: gt, lt
  assign out = {{15{1'b0}}, comparator_1_eq};  // Bit_Extender bit_extender_1
endmodule
