// Logisim project regfile.circ as structural Verilog: 1 circuit, main circuit main
module main (
  input  [2:0] Read_Register_1,
  input  [2:0] Read_Register_2,
  input  [2:0] Write_Register,
  input  [15:0] Write_Data,
  input  Write_Enable,
  input  Clock,
  output [15:0] s0_Value,
  output [15:0] s1_Value,
  output [15:0] s2_Value,
  output [15:0] ra_Value,
  output [15:0] sp_Value,
  output [15:0] Read_Data_1,
  output [15:0] Read_Data_2
);

  wire decoder_1_out1, decoder_1_out2, decoder_1_out3, decoder_1_out4, decoder_1_out5, decoder_1_out6,
       decoder_1_out7;
  wire [15:0] _0_q, a0_q, demultiplexer_1_out0, demultiplexer_1_out2, demultiplexer_1_out3,
       demultiplexer_1_out4, demultiplexer_1_out5, demultiplexer_1_out6, demultiplexer_1_out7, RA_t, v0_q;

  Demultiplexer #(.select(3), .width(16)) demultiplexer_1 (
    .out0(demultiplexer_1_out0), .out1(RA_t), .out2(demultiplexer_1_out2), .out3(demultiplexer_1_out3),
    .out4(demultiplexer_1_out4), .out5(demultiplexer_1_out5), .out6(demultiplexer_1_out6),
    .out7(demultiplexer_1_out7), .in(Write_Data), .sel(Write_Register), .en(Write_Enable));
  Decoder #(.select(3)) decoder_1 (
    .out1(decoder_1_out1), .out2(decoder_1_out2), .out3(decoder_1_out3), .out4(decoder_1_out4),
    .out5(decoder_1_out5), .out6(decoder_1_out6), .out7(decoder_1_out7), .sel(Write_Register),
    .en(Write_Enable));  // open: out0
  Register #(.width(16)) _0 (.D(demultiplexer_1_out0), .en(1'b0), .Q(_0_q), .clk(Clock));  // open: clr
  Register #(.width(16)) ra (.D(RA_t), .en(decoder_1_out1), .Q(ra_Value), .clk(Clock));  // open: clr
  Register #(.width(16)) s0 (.D(demultiplexer_1_out2), .en(decoder_1_out2), .Q(s0_Value), .clk(Clock));  // open: clr
  Register #(.width(16)) s1 (.D(demultiplexer_1_out3), .en(decoder_1_out3), .Q(s1_Value), .clk(Clock));  // open: clr
  Register #(.width(16)) s2 (.D(demultiplexer_1_out4), .en(decoder_1_out4), .Q(s2_Value), .clk(Clock));  // open: clr
  Register #(.width(16)) a0 (.D(demultiplexer_1_out5), .en(decoder_1_out5), .Q(a0_q), .clk(Clock));  // open: clr
  Register #(.width(16)) v0 (.D(demultiplexer_1_out6), .en(decoder_1_out6), .Q(v0_q), .clk(Clock));  // open: clr
  Register #(.width(16)) sp (.D(demultiplexer_1_out7), .en(decoder_1_out7), .Q(sp_Value), .clk(Clock));  // open: clr
  Multiplexer #(.select(3), .width(16)) multiplexer_1 (
    .in0(_0_q), .in1(ra_Value), .in2(s0_Value), .in3(s1_Value), .in4(s2_Value), .in5(a0_q), .in6(v0_q),
    .in7(sp_Value), .out(Read_Data_1), .sel(Read_Register_1));  // open: en
  Multiplexer #(.select(3), .width(16)) multiplexer_2 (
    .in0(_0_q), .in1(ra_Value), .in2(s0_Value), .in3(s1_Value), .in4(s2_Value), .in5(a0_q), .in6(v0_q),
    .in7(sp_Value), .out(Read_Data_2), .sel(Read_Register_2));  // open: en

  // Other names for the same wires on the sheet: clk = Clock; ra[15:0] = ra_Value; read_data1[15:0] = Read_Data_1;
  //   read_data2[15:0] = Read_Data_2; read_reg1[2:0] = Read_Register_1; read_reg2[2:0] = Read_Register_2;
  //   s0[15:0] = s0_Value; s1[15:0] = s1_Value; s2[15:0] = s2_Value; sp[15:0] = sp_Value; write_en = Write_Enable;
  //   write_reg[2:0] = Write_Register

  // Notes on the sheet:
  //   INPUTS to your circuit
  //   DON'T CHANGE THE LOCATIONS OF THE INPUTS AND OUTPUTS!
  //   These are DEBUG/TEST outputs from your circuit.
  //   OUTPUTS from your circuit
endmodule
