// Logisim project alu.circ as structural Verilog: 9 circuits, main circuit main
module main (
  input  [15:0] X,
  input  [15:0] Y,
  input  [2:0] Switch,
  output Equal,
  output [15:0] Result,
  output [15:0] Result_2,
  output Signed_Overflow
);

  wire add_overflow, comparator_1_eq, comparator_2_eq;
  wire [15:0] add_out, addu_out, and_out, lower16, or_out, sll_out, slt_out, srl_out, upper16;

  sll sll (.input1(X), .input2(Y), .out(sll_out));
  srl srl (.input1(X), .input2(Y), .out(srl_out));
  add add (.inp1(X), .inp2(Y), .overflow(add_overflow), .out(add_out));
  \and  \and  (.inp1(X), .inp2(Y), .out(and_out));
  \or  \or  (.inp1(X), .inp2(Y), .out(or_out));
  addu addu (.inp1(X), .inp2(Y), .out(addu_out));
  slt slt (.inp1(X), .inp2(Y), .out(slt_out));
  mult mult (.inp1(X), .inp2(Y), .Result(lower16), .Result2(upper16));
  Comparator #(.width(3)) comparator_1 (.a(3'b111), .b(Switch), .eq(comparator_1_eq));  // open: gt, lt
  Comparator #(.width(3)) comparator_2 (.a(3'b010), .b(Switch), .eq(comparator_2_eq));  // open: gt, lt
  Multiplexer #(.width(16)) multiplexer_1 (
    .in0({16{1'b0}}), .in1(upper16), .out(Result_2), .sel(comparator_1_eq));  // open: en
  Multiplexer #(.select(3), .width(16), .enable("false")) multiplexer_2 (
    .in0(sll_out), .in1(srl_out), .in2(add_out), .in3(and_out), .in4(or_out), .in5(addu_out), .in6(slt_out),
    .in7(lower16), .out(Result), .sel(Switch));
  and and_2 (Signed_Overflow, comparator_2_eq, add_overflow);
  Comparator #(.width(16)) comparator_3 (.a(X), .b(Y), .eq(Equal));  // open: gt, lt

  // Other names for the same wires on the sheet: overflow = Signed_Overflow; S[2:0] = Switch

  // Notes on the sheet:
  //   INPUTS to your circuit
  //   DON'T CHANGE THE LOCATIONS OF THE INPUTS AND OUTPUTS!
  //   OUTPUTS from your circuit
endmodule

module sll (
  input  [15:0] input1,
  input  [15:0] input2,
  output [15:0] out
);

  wire [3:0] bit_extender_1_out;

  Bit_Extender #(.in_width(16), .out_width(4)) bit_extender_1 (.in(input2), .out(bit_extender_1_out));
  Shifter #(.width(16)) shifter_1 (.in(input1), .\dist (bit_extender_1_out), .out(out));
endmodule

module srl (
  input  [15:0] input1,
  input  [15:0] input2,
  output [15:0] out
);

  wire [3:0] bit_extender_1_out;

  Bit_Extender #(.in_width(16), .out_width(4)) bit_extender_1 (.in(input2), .out(bit_extender_1_out));
  Shifter #(.width(16), .shift("lr")) shifter_1 (.in(input1), .\dist (bit_extender_1_out), .out(out));
endmodule

module add (
  input  [15:0] inp1,
  input  [15:0] inp2,
  output [15:0] out,
  output overflow
);

  wire and_1_out, and_2_out, and_3_out, and_4_out, not_1_out, not_2_out, not_3_out;

  not not_1 (not_1_out, inp1[15]);
  not not_2 (not_2_out, inp2[15]);
  Adder #(.width(16)) adder_1 (.a(inp1), .b(inp2), .out(out));  // open: cin, cout
  and and_1 (and_1_out, not_1_out, not_2_out);
  and and_2 (and_2_out, inp1[15], inp2[15]);
  and and_3 (and_3_out, and_1_out, out[15]);
  not not_3 (not_3_out, out[15]);
  and and_4 (and_4_out, not_3_out, and_2_out);
  or or_1 (overflow, and_4_out, and_3_out);
endmodule

module \and  (
  input  [15:0] inp1,
  input  [15:0] inp2,
  output [15:0] out
);

  assign out = inp1 & inp2;  // AND_Gate and_1, 16 bits wide
endmodule

module \or  (
  input  [15:0] inp1,
  input  [15:0] inp2,
  output [15:0] out
);

  assign out = inp1 | inp2;  // OR_Gate or_1, 16 bits wide
endmodule

module addu (
  input  [15:0] inp1,
  input  [15:0] inp2,
  output [15:0] out
);

  Adder #(.width(16)) adder_1 (.a(inp1), .b(inp2), .out(out));  // open: cin, cout
endmodule

module slt (
  input  [15:0] inp1,
  input  [15:0] inp2,
  output [15:0] out
);

  wire comparator_1_lt;

  Comparator #(.width(16)) comparator_1 (.a(inp1), .b(inp2), .lt(comparator_1_lt));  // open: gt, eq
  assign out = {{15{1'b0}}, comparator_1_lt};  // Bit_Extender bit_extender_1
endmodule

module mult (
  input  [15:0] inp1,
  input  [15:0] inp2,
  output [15:0] Result,
  output [15:0] Result2
);

  wire [31:0] bit_extender_1_out, bit_extender_2_out;

  assign bit_extender_1_out = {{16{1'b0}}, inp1};  // Bit_Extender bit_extender_1
  assign bit_extender_2_out = {{16{1'b0}}, inp2};  // Bit_Extender bit_extender_2
  Multiplier #(.width(32)) multiplier_1 (
    .a(bit_extender_1_out), .b(bit_extender_2_out), .out({Result2, Result}));  // open: cin, cout
endmodule
