// Logisim project cpu.circ as structural Verilog: 2 circuits, main circuit main
module main (
  input  [15:0] INSTRUCTION,
  input  CLOCK,
  output [15:0] FETCH_ADDRESS,
  output [15:0] s0_Value,
  output [15:0] s1_Value,
  output [15:0] s2_Value,
  output [15:0] ra_Value,
  output [15:0] sp_Value,
  output [15:0] HI_Value,
  output [15:0] LO_Value
);

  wire alu_src, and_1_out, and_2_out, beq, bne, equal, ext_op, is_branch, jal, jalr, kill, lui, MEM_p1,
       MEM_p2, MEM_p4, MEM_p10, memToReg, memWrite, mfhi, mflo, mult, not_1_out, or_4_out, or_5_out,
       reg_write, take_branch, write_lo;
  wire [2:0] alu_op, bit_extender_1_out, FUNCT, multiplexer_3_out, multiplexer_4_out;
  wire [2:1] RD;
  wire [3:0] OPCODE;
  wire [5:3] IMM6;
  wire [9:0] oldPC_q;
  wire [9:6] IMM10;
  wire [15:0] alu_out, bit_extender_2_out, bit_extender_3_out, BranchAddr, IMM6_EXT, memOut,
       multiplexer_1_out, multiplexer_2_out, multiplexer_7_out, multiplexer_8_out, multiplexer_9_out,
       multiplexer_10_out, multiplexer_11_out, multiplexer_12_out, PC_2, read_reg1, read_reg2, result2,
       write_data, Y;
  wire [15:10] JalAddr;

  Multiplexer #(.width(16)) multiplexer_1 (
    .in0(alu_out), .in1({IMM10, IMM6, FUNCT, {6{1'b0}}}), .out(multiplexer_1_out), .sel(lui));  // open: en
  Multiplexer #(.width(16)) multiplexer_2 (
    .in0(INSTRUCTION), .in1({16{1'b0}}), .out(multiplexer_2_out), .sel(kill));  // open: en
  or or_1 (kill, take_branch, jal, jalr);
  not not_1 (not_1_out, equal);
  Register #(.width(16)) LO (.D(multiplexer_1_out), .en(write_lo), .Q(LO_Value), .clk(CLOCK));  // open: clr
  Register #(.width(16)) HI (.D(result2), .en(mult), .Q(HI_Value), .clk(CLOCK));  // open: clr
  Register #(.width(16)) register_1 (
    .D(multiplexer_2_out), .Q({OPCODE, RD, IMM10, IMM6, FUNCT}), .clk(CLOCK));  // open: en, clr
  or or_2 (is_branch, beq, bne);
  and and_1 (and_1_out, bne, not_1_out);
  or or_3 (take_branch, and_1_out, and_2_out);
  and and_2 (and_2_out, beq, equal);
  assign bit_extender_1_out = {{1{1'b0}}, RD};  // Bit_Extender bit_extender_1
  Multiplexer #(.width(3)) multiplexer_3 (
    .in0(IMM6), .in1({RD, IMM10[9]}), .out(multiplexer_3_out), .sel(or_4_out));  // open: en
  or or_4 (or_4_out, is_branch, memWrite);
  Multiplexer #(.width(3)) multiplexer_4 (
    .in0({RD, IMM10[9]}), .in1(bit_extender_1_out), .out(multiplexer_4_out), .sel(jal));  // open: en
  assign bit_extender_2_out = {{10{1'b0}}, {IMM6, FUNCT}};  // Bit_Extender bit_extender_2
  assign bit_extender_3_out = {{10{IMM6[5]}}, {IMM6, FUNCT}};  // Bit_Extender bit_extender_3
  alu_main main_1 (.Switch(alu_op), .X(read_reg1), .Equal(equal), .Result(alu_out), .Y(Y), .Result_2(result2));
  Multiplexer #(.width(16)) multiplexer_5 (
    .in0(bit_extender_2_out), .in1(bit_extender_3_out), .out(IMM6_EXT), .sel(ext_op));  // open: en
  control control_1 (
    .opcode(OPCODE), .funct(FUNCT), .alu_op(alu_op), .memWrite(memWrite), .alu_src(alu_src),
    .write_reg(reg_write), .ext_op(ext_op), .MemToReg(memToReg), .jal(jal), .bne(bne), .beq(beq),
    .jalr(jalr), .write_lo(write_lo), .lui(lui), .mult(mult), .mflo(mflo), .mfhi(mfhi));
  regfile_main main_2 (
    .Read_Register_1(IMM10[8:6]), .Read_Register_2(multiplexer_3_out), .Write_Register(multiplexer_4_out),
    .Write_Data(write_data), .Write_Enable(reg_write), .Clock(CLOCK), .Read_Data_1(read_reg1),
    .Read_Data_2(read_reg2), .s0_Value(s0_Value), .s1_Value(s1_Value), .s2_Value(s2_Value),
    .ra_Value(ra_Value), .sp_Value(sp_Value));
  Multiplexer #(.width(16)) multiplexer_6 (.in0(read_reg2), .in1(IMM6_EXT), .out(Y), .sel(alu_src));  // open: en
  Multiplexer #(.width(16)) multiplexer_7 (
    .in0(PC_2), .in1(BranchAddr), .out(multiplexer_7_out), .sel(take_branch));  // open: en
  Multiplexer #(.width(16)) multiplexer_8 (
    .in0(multiplexer_7_out), .in1(alu_out), .out(multiplexer_8_out), .sel(jalr));  // open: en
  Multiplexer #(.width(16)) multiplexer_9 (
    .in0(multiplexer_8_out), .in1({JalAddr, IMM10, IMM6, FUNCT}), .out(multiplexer_9_out), .sel(jal));  // open: en
  // Probe on multiplexer_9_out
  Register #(.width(16)) PC (.D(multiplexer_9_out), .Q(FETCH_ADDRESS), .clk(CLOCK));  // open: en, clr
  Register #(.width(16)) oldPC (.D(FETCH_ADDRESS), .Q({JalAddr, oldPC_q}), .clk(CLOCK));  // open: en, clr
  Multiplexer #(.width(16)) multiplexer_10 (
    .in0(alu_out), .in1(memOut), .out(multiplexer_10_out), .sel(memToReg));  // open: en
  Multiplexer #(.width(16)) multiplexer_11 (
    .in0(multiplexer_10_out), .in1(LO_Value), .out(multiplexer_11_out), .sel(mflo));  // open: en
  // mem_main MEM: pin names not known; wires that end beside it: MEM_p1, MEM_p2, MEM_p2, MEM_p4, alu_out, read_reg2, memWrite, MEM_p4, CLOCK, MEM_p10, memOut
  Adder #(.width(16)) adder_1 (.a(16'h2), .b(FETCH_ADDRESS), .out(PC_2));  // open: cin, cout
  Multiplexer #(.width(16)) multiplexer_12 (
    .in0(multiplexer_11_out), .in1(HI_Value), .out(multiplexer_12_out), .sel(mfhi));  // open: en
  Multiplexer #(.width(16)) multiplexer_13 (
    .in0(multiplexer_12_out), .in1(FETCH_ADDRESS), .out(write_data), .sel(or_5_out));  // open: en
  or or_5 (or_5_out, jal, jalr);
  Adder #(.width(16)) adder_2 (.a({JalAddr, oldPC_q}), .b(IMM6_EXT), .out(BranchAddr));  // open: cin, cout

  // Other names for the same wires on the sheet: RD2[1:0] = RD; clk = CLOCK; fetch_addr[15:0] = FETCH_ADDRESS;
  //   hi[15:0] = HI_Value; IMM6[2:0] = FUNCT; IMM10[5:0] = {IMM6, FUNCT}; IMM10_SHIFT[15:6] = {IMM10, IMM6, FUNCT};
  //   JalAddr[9:0] = {IMM10, IMM6, FUNCT}; RT[2:0] = IMM6; RS[2:0] = IMM10[8:6]; RD[0] = IMM10[9];
  //   lo[15:0] = LO_Value; ra[15:0] = ra_Value; X[15:0] = read_reg1; s0[15:0] = s0_Value; s1[15:0] = s1_Value;
  //   s2[15:0] = s2_Value; sp[15:0] = sp_Value

  // Notes on the sheet:
  //   Output
  //   These are outputs/inputs from run.circ
  //   Inputs
  //   EX
  //   REGFILE
  //   These are DEBUG/TEST outputs from your circuit.
  //   PC
  //   MEM
  //   WB
endmodule

module control (
  input  [3:0] opcode,
  input  [2:0] funct,
  output memWrite,
  output alu_src,
  output jal,
  output bne,
  output beq,
  output jalr,
  output write_lo,
  output lui,
  output mult,
  output mflo,
  output mfhi,
  output write_reg,
  output ext_op,
  output MemToReg,
  output [2:0] alu_op
);

  wire andi, comparator_12_eq, ori, rtype, sw;
  wire [2:0] multiplexer_1_out;

  Multiplexer #(.select(4), .width(3)) multiplexer_1 (
    .in0(3'b000), .in1(3'b000), .in2(3'b000), .in3(3'b010), .in4(3'b000), .in5(3'b000), .in6(3'b010),
    .in7(3'b110), .in8(3'b011), .in9(3'b100), .in10(3'b010), .in11(3'b010), .in12(3'b000), .in13(3'b000),
    .in14(3'b000), .in15(3'b000), .out(multiplexer_1_out), .sel(opcode));  // open: en
  Comparator #(.width(4), .mode("unsigned")) comparator_1 (.a(opcode), .b(4'b1011), .eq(sw));  // open: gt, lt
  Comparator #(.width(4), .mode("unsigned")) comparator_2 (.a(opcode), .b(4'b1000), .eq(andi));  // open: gt, lt
  Comparator #(.width(4), .mode("unsigned")) comparator_3 (.a(opcode), .b(4'b1001), .eq(ori));  // open: gt, lt
  Comparator #(.width(4), .mode("unsigned")) comparator_4 (.a(opcode), .b(4'b1010), .eq(MemToReg));  // open: gt, lt
  Multiplexer #(.width(3)) multiplexer_2 (.in0(multiplexer_1_out), .in1(funct), .out(alu_op), .sel(rtype));  // open: en
  or or_1 (write_lo, mult, lui);
  nor nor_1 (write_reg, mult, lui, bne, sw, beq);
  nor nor_2 (ext_op, ori, andi);
  nor nor_3 (alu_src, rtype, beq, bne);
  Comparator #(.width(4), .mode("unsigned")) comparator_5 (.a(opcode), .b(4'b0100), .eq(beq));  // open: gt, lt
  Comparator #(.width(4), .mode("unsigned")) comparator_6 (.a(opcode), .b(4'b0101), .eq(bne));  // open: gt, lt
  Comparator #(.width(4), .mode("unsigned")) comparator_7 (.a(opcode), .b(4'b0010), .eq(jal));  // open: gt, lt
  Comparator #(.width(4), .mode("unsigned")) comparator_8 (.a(opcode), .b(4'b0011), .eq(jalr));  // open: gt, lt
  Comparator #(.width(4), .mode("unsigned")) comparator_9 (.a(opcode), .b(4'b0001), .eq(lui));  // open: gt, lt
  Comparator #(.width(4), .mode("unsigned")) comparator_10 (.a(opcode), .b(4'b1101), .eq(mflo));  // open: gt, lt
  Comparator #(.width(4), .mode("unsigned")) comparator_11 (.a(opcode), .b(4'b1100), .eq(mfhi));  // open: gt, lt
  Comparator #(.width(3), .mode("unsigned")) comparator_12 (
    .a(funct), .b(3'b111), .eq(comparator_12_eq));  // open: gt, lt
  and and_1 (mult, comparator_12_eq, rtype);
  Comparator #(.width(4), .mode("unsigned")) comparator_13 (.a(opcode), .b(4'b0000), .eq(rtype));  // open: gt, lt
  Comparator #(.width(4), .mode("unsigned")) comparator_14 (.a(opcode), .b(4'b1011), .eq(memWrite));  // open: gt, lt

  // Other names for the same wires on the sheet: load = MemToReg
endmodule
