// Logisim project regfile.circ as structural Verilog: 1 circuit, main circuit main
module main (
  input  [2:0] Read_Register_1,
  input  [2:0] Read_Register_2,
  input  [2:0] Write_Register,
  input  [15:0] Write_Data,
  input  Write_Enable,
  input  Clock,
  output [15:0] s0_Value,
  output [15:0] s1_Value,
  output [15:0] s2_Value,
  output [15:0] ra_Value,
  output [15:0] sp_Value,
  output [15:0] Read_Data_1,
  output [15:0] Read_Data_2
);

  wire en0, en1, en2, en3, en4, en5, en6, en7;
  wire [15:0] x0, x5, x6;

  Demultiplexer #(.select(3)) demultiplexer_1 (
    .out0(en0), .out1(en1), .out2(en2), .out3(en3), .out4(en4), .out5(en5), .out6(en6), .out7(en7),
    .in(Write_Enable), .sel(Write_Register));  // open: en
  Register #(.width(16)) u_x0 (.D({16{1'b0}}), .en(1'b0), .Q(x0), .clk(Clock));  // open: clr
  Register #(.width(16)) x4 (.D(Write_Data), .en(en4), .Q(s2_Value), .clk(Clock));  // open: clr
  Multiplexer #(.select(3), .width(16)) multiplexer_1 (
    .in0(x0), .in1(ra_Value), .in2(s0_Value), .in3(s1_Value), .in4(s2_Value), .in5(x5), .in6(x6),
    .in7(sp_Value), .out(Read_Data_1), .sel(Read_Register_1));  // open: en
  Register #(.width(16)) x1 (.D(Write_Data), .en(en1), .Q(ra_Value), .clk(Clock));  // open: clr
  Register #(.width(16)) u_x5 (.D(Write_Data), .en(en5), .Q(x5), .clk(Clock));  // open: clr
  Multiplexer #(.select(3), .width(16)) multiplexer_2 (
    .in0(x0), .in1(ra_Value), .in2(s0_Value), .in3(s1_Value), .in4(s2_Value), .in5(x5), .in6(x6),
    .in7(sp_Value), .out(Read_Data_2), .sel(Read_Register_2));  // open: en
  Register #(.width(16)) x2 (.D(Write_Data), .en(en2), .Q(s0_Value), .clk(Clock));  // open: clr
  Register #(.width(16)) u_x6 (.D(Write_Data), .en(en6), .Q(x6), .clk(Clock));  // open: clr
  Register #(.width(16)) x3 (.D(Write_Data), .en(en3), .Q(s1_Value), .clk(Clock));  // open: clr
  Register #(.width(16)) x7 (.D(Write_Data), .en(en7), .Q(sp_Value), .clk(Clock));  // open: clr

  // Other names for the same wires on the sheet: clk = Clock; read_data1[15:0] = Read_Data_1;
  //   read_data2[15:0] = Read_Data_2; read_reg1[2:0] = Read_Register_1; read_reg2[2:0] = Read_Register_2;
  //   write_en = Write_Enable; write_reg[2:0] = Write_Register; x1[15:0] = ra_Value; x2[15:0] = s0_Value;
  //   x3[15:0] = s1_Value; x4[15:0] = s2_Value; x7[15:0] = sp_Value

  // Notes on the sheet:
  //   INPUTS to your circuit
  //   DON'T CHANGE THE LOCATIONS OF THE INPUTS AND OUTPUTS!
  //   These are DEBUG/TEST outputs from your circuit.
  //   OUTPUTS from your circuit
endmodule
