// Logisim project regfile.circ as structural Verilog: 1 circuit, main circuit main
module main (
  input  [2:0] Read_Register_1,
  input  [2:0] Read_Register_2,
  input  [2:0] Write_Register,
  input  [15:0] Write_Data,
  input  Write_Enable,
  input  Clock,
  output [15:0] s0_Value,
  output [15:0] s1_Value,
  output [15:0] s2_Value,
  output [15:0] ra_Value,
  output [15:0] sp_Value,
  output [15:0] Read_Data_1,
  output [15:0] Read_Data_2
);

  wire _0_write, a0_write, and_1_out, and_2_out, and_3_out, and_4_out, and_5_out, and_6_out, and_7_out,
       and_8_out, ra_write, s0_write, s1_write, s2_write, sp_write, v0_write;
  wire [15:0] _0_out, a0_out, multiplexer_2_out, multiplexer_3_out, v0_out;

  Demultiplexer #(.select(3), .enable("false")) demultiplexer_1 (
    .out0(_0_write), .out1(ra_write), .out2(s0_write), .out3(s1_write), .out4(s2_write), .out5(a0_write),
    .out6(v0_write), .out7(sp_write), .in(1'b1), .sel(Write_Register));
  and and_1 (and_1_out, s2_write, Write_Enable);
  and and_2 (and_2_out, v0_write, Write_Enable);
  Multiplexer #(.select(3), .width(16), .enable("false")) multiplexer_1 (
    .in0(_0_out), .in1(ra_Value), .in2(s0_Value), .in3(s1_Value), .in4(s2_Value), .in5(a0_out), .in6(v0_out),
    .in7(sp_Value), .out(Read_Data_2), .sel(Read_Register_2));
  and and_3 (and_3_out, _0_write, Write_Enable);
  and and_4 (and_4_out, ra_write, Write_Enable);
  Register #(.width(16)) s2 (.D(Write_Data), .en(and_1_out), .Q(s2_Value), .clk(Clock));  // open: clr
  Register #(.width(16)) v0 (.D(Write_Data), .en(and_2_out), .Q(v0_out), .clk(Clock));  // open: clr
  Register #(.width(16)) _0 (.D(multiplexer_2_out), .Q(_0_out), .clk(Clock));  // open: en, clr
  Multiplexer #(.width(16), .enable("false")) multiplexer_2 (
    .in0({16{1'b0}}), .in1({16{1'b0}}), .out(multiplexer_2_out), .sel(and_3_out));
  Register #(.width(16)) ra (.D(Write_Data), .en(and_4_out), .Q(ra_Value), .clk(Clock));  // open: clr
  and and_5 (and_5_out, s0_write, Write_Enable);
  and and_6 (and_6_out, s1_write, Write_Enable);
  and and_7 (and_7_out, a0_write, Write_Enable);
  and and_8 (and_8_out, sp_write, Write_Enable);
  Register #(.width(16)) s0 (.D(Write_Data), .en(and_5_out), .Q(s0_Value), .clk(Clock));  // open: clr
  Register #(.width(16)) s1 (.D(multiplexer_3_out), .Q(s1_Value), .clk(Clock));  // open: en, clr
  Multiplexer #(.width(16), .enable("false")) multiplexer_3 (
    .in0(s1_Value), .in1(Write_Data), .out(multiplexer_3_out), .sel(and_6_out));
  Register #(.width(16)) a0 (.D(Write_Data), .en(and_7_out), .Q(a0_out), .clk(Clock));  // open: clr
  Register #(.width(16)) sp (.D(Write_Data), .en(and_8_out), .Q(sp_Value), .clk(Clock));  // open: clr
  Multiplexer #(.select(3), .width(16), .enable("false")) multiplexer_4 (
    .in0(_0_out), .in1(ra_Value), .in2(s0_Value), .in3(s1_Value), .in4(s2_Value), .in5(a0_out), .in6(v0_out),
    .in7(sp_Value), .out(Read_Data_1), .sel(Read_Register_1));

  // Other names for the same wires on the sheet: clk = Clock; ra_out[15:0] = ra_Value; read_data1[15:0] = Read_Data_1;
  //   read_data2[15:0] = Read_Data_2; read_reg1[2:0] = Read_Register_1; read_reg2[2:0] = Read_Register_2;
  //   s0_out[15:0] = s0_Value; s1_out[15:0] = s1_Value; s2_out[15:0] = s2_Value; sp_out[15:0] = sp_Value;
  //   write_en = Write_Enable; write_reg[2:0] = Write_Register

  // Notes on the sheet:
  //   INPUTS to your circuit
  //   DON'T CHANGE THE LOCATIONS OF THE INPUTS AND OUTPUTS!
  //   These are DEBUG/TEST outputs from your circuit.
  //   OUTPUTS from your circuit
endmodule
